# Fritzing sketch L24 - Fritzing simple (saved by Fritzing 0.9.2b)
breadboards: 1

parts:
  LCD1 = LCD screen
  U1 = POT [package=pot_alpha_rv16af-20]
  Part1 = Arduino Uno (Rev3)

nets:
  VSS: LCD1.VSS, LCD1.R/W, LCD1.LED-, U1.A, Part1.GND
  VDD: LCD1.VDD, LCD1.LED+, U1.E, Part1.5V
  N1: LCD1.V0, U1.S
  N2: LCD1.RS, Part1.D12/MISO
  N3: LCD1.E, Part1.D11_PWM/MOSI
  N4: LCD1.DB4, Part1.D5_PWM
  N5: LCD1.DB5, Part1.D4
  N6: LCD1.DB6, Part1.D3_PWM
  N7: LCD1.DB7, Part1.D2
