# Fritzing sketch L24 - LCD character screen DHT22 (saved by Fritzing 0.9.2b)
breadboards: 1

parts:
  LCD2 = LCD screen
  U2 = POT [package=pot_alpha_rv16af-20]
  RHT1 = Humidity and Temperature Sensor RHT03  # not connected
  Part2 = Arduino Uno (Rev3)

nets:
  VSS: LCD2.VSS, LCD2.R/W, LCD2.LED-, U2.A, Part2.GND
  VDD: LCD2.VDD, LCD2.LED+, U2.E, Part2.5V
  N1: LCD2.V0, U2.S
  N2: LCD2.RS, Part2.D12/MISO
  N3: LCD2.E, Part2.D11_PWM/MOSI
  N4: LCD2.DB4, Part2.D5_PWM
  N5: LCD2.DB5, Part2.D4
  N6: LCD2.DB6, Part2.D3_PWM
  N7: LCD2.DB7, Part2.D2
